// Logisim project ALU.circ as structural Verilog: 11 circuits, main circuit ALU32
module LeftShift32 (
  input  [31:0] B,
  input  Cin,
  input  [4:0] Sa,
  output [31:0] C
);

  wire [31:0] eight_bit_shifter_1_shifted, four_bit_shifter_1_shifted, multiplexer_1_out, multiplexer_2_out,
       multiplexer_3_out, multiplexer_4_out, one_bit_shifter_1_shifted, sixteen_bit_shifter_1_shifted,
       two_bit_shifter_1_shifted;

  one_bit_shifter one_bit_shifter_1 (.C_in(Cin), .B(B), .shifted(one_bit_shifter_1_shifted));
  Multiplexer #(.width(32), .enable("false")) multiplexer_1 (
    .in0(B), .in1(one_bit_shifter_1_shifted), .out(multiplexer_1_out), .sel(Sa[0]));
  Multiplexer #(.width(32), .enable("false")) multiplexer_2 (
    .in0(multiplexer_1_out), .in1(two_bit_shifter_1_shifted), .out(multiplexer_2_out), .sel(Sa[1]));
  two_bit_shifter two_bit_shifter_1 (.C_in(Cin), .B(multiplexer_1_out), .shifted(two_bit_shifter_1_shifted));
  Multiplexer #(.width(32), .enable("false")) multiplexer_3 (
    .in0(multiplexer_2_out), .in1(four_bit_shifter_1_shifted), .out(multiplexer_3_out), .sel(Sa[2]));
  four_bit_shifter four_bit_shifter_1 (.C_in(Cin), .B(multiplexer_2_out), .shifted(four_bit_shifter_1_shifted));
  eight_bit_shifter eight_bit_shifter_1 (.C_in(Cin), .B(multiplexer_3_out), .shifted(eight_bit_shifter_1_shifted));
  Multiplexer #(.width(32), .enable("false")) multiplexer_4 (
    .in0(multiplexer_3_out), .in1(eight_bit_shifter_1_shifted), .out(multiplexer_4_out), .sel(Sa[3]));
  sixteen_bit_shifter sixteen_bit_shifter_1 (
    .C_in(Cin), .B(multiplexer_4_out), .Shifted(sixteen_bit_shifter_1_shifted));
  Multiplexer #(.width(32), .enable("false")) multiplexer_5 (
    .in0(multiplexer_4_out), .in1(sixteen_bit_shifter_1_shifted), .out(C), .sel(Sa[4]));

  // Notes on the sheet:
  //   left 32 bit shifter
endmodule

module ALU32 (
  input  [31:0] A,
  input  [31:0] B,
  input  [3:0] Op,
  input  [4:0] Sa,
  output [31:0] C,
  output V
);


  // Notes on the sheet:
  //   Do not delete or rename any of the input or output pins, and do not add any other pins.
  //   (It's fine to move the pins around, though)
endmodule

module one_bit_shifter (
  input  C_in,
  input  [31:0] B,
  output [31:0] shifted
);


  assign shifted = {B[30:0], C_in};

  // Notes on the sheet:
  //   one bit shifter
endmodule

module Add32 (
  input  [31:0] A,
  input  [31:0] B,
  input  Cin,
  output V,
  output [31:0] C
);

  wire four_bit_adder_1_cout, four_bit_adder_2_cout, four_bit_adder_3_cout, four_bit_adder_4_cout,
       four_bit_adder_5_cout, four_bit_adder_6_cout, four_bit_adder_7_cout;

  four_bit_adder four_bit_adder_1 (
    .A4(B[31:28]), .B4(A[31:28]), .Cin(Cin), .Cout(four_bit_adder_1_cout), .S4(C[31:28]));
  four_bit_adder four_bit_adder_2 (
    .A4(B[27:24]), .B4(A[27:24]), .Cin(four_bit_adder_1_cout), .Cout(four_bit_adder_2_cout), .S4(C[27:24]));
  four_bit_adder four_bit_adder_3 (
    .A4(B[23:20]), .B4(A[23:20]), .Cin(four_bit_adder_2_cout), .Cout(four_bit_adder_3_cout), .S4(C[23:20]));
  four_bit_adder four_bit_adder_4 (
    .A4(B[19:16]), .B4(A[19:16]), .Cin(four_bit_adder_3_cout), .Cout(four_bit_adder_4_cout), .S4(C[19:16]));
  four_bit_adder four_bit_adder_5 (
    .A4(B[15:12]), .B4(A[15:12]), .Cin(four_bit_adder_4_cout), .Cout(four_bit_adder_5_cout), .S4(C[15:12]));
  four_bit_adder four_bit_adder_6 (
    .A4(B[11:8]), .B4(A[11:8]), .Cin(four_bit_adder_5_cout), .Cout(four_bit_adder_6_cout), .S4(C[11:8]));
  four_bit_adder four_bit_adder_7 (
    .A4(B[7:4]), .B4(A[7:4]), .Cin(four_bit_adder_6_cout), .Cout(four_bit_adder_7_cout), .S4(C[7:4]));
  four_bit_adder four_bit_adder_8 (.A4(B[3:0]), .B4(A[3:0]), .Cin(four_bit_adder_7_cout), .Cout(V), .S4(C[3:0]));
endmodule

module two_bit_shifter (
  input  C_in,
  input  [31:0] B,
  output [31:0] shifted
);

  wire [31:0] one_bit_shifter_1_shifted;

  one_bit_shifter one_bit_shifter_1 (.C_in(C_in), .B(B), .shifted(one_bit_shifter_1_shifted));
  one_bit_shifter one_bit_shifter_2 (.C_in(C_in), .B(one_bit_shifter_1_shifted), .shifted(shifted));

  // Notes on the sheet:
  //   two bit shifter
endmodule

module four_bit_shifter (
  input  C_in,
  input  [31:0] B,
  output [31:0] shifted
);

  wire [31:0] two_bit_shifter_1_shifted;

  two_bit_shifter two_bit_shifter_1 (.C_in(C_in), .B(B), .shifted(two_bit_shifter_1_shifted));
  two_bit_shifter two_bit_shifter_2 (.C_in(C_in), .B(two_bit_shifter_1_shifted), .shifted(shifted));

  // Notes on the sheet:
  //   four bit shifter
endmodule

module eight_bit_shifter (
  input  C_in,
  input  [31:0] B,
  output [31:0] shifted
);

  wire [31:0] four_bit_shifter_1_shifted;

  four_bit_shifter four_bit_shifter_1 (.C_in(C_in), .B(B), .shifted(four_bit_shifter_1_shifted));
  four_bit_shifter four_bit_shifter_2 (.C_in(C_in), .B(four_bit_shifter_1_shifted), .shifted(shifted));

  // Notes on the sheet:
  //   eight bit shifter
endmodule

module sixteen_bit_shifter (
  input  C_in,
  input  [31:0] B,
  output [31:0] Shifted
);

  wire [31:0] eight_bit_shifter_1_shifted;

  eight_bit_shifter eight_bit_shifter_1 (.C_in(C_in), .B(B), .shifted(eight_bit_shifter_1_shifted));
  eight_bit_shifter eight_bit_shifter_2 (.C_in(C_in), .B(eight_bit_shifter_1_shifted), .shifted(Shifted));

  // Notes on the sheet:
  //   sixteen bit shifter
endmodule

module one_bit_adder (
  input  A,
  input  B,
  input  Cin,
  output S,
  output Cout
);

  wire and_1_out, and_2_out, xor_1_out;

  xor xor_1 (xor_1_out, A, B);
  and and_1 (and_1_out, xor_1_out, Cin);
  and and_2 (and_2_out, A, B);
  xor xor_2 (S, xor_1_out, Cin);
  or or_1 (Cout, and_1_out, and_2_out);

  // Notes on the sheet:
  //   1-bit adder
endmodule

module four_bit_adder (
  input  [3:0] A4,
  input  [3:0] B4,
  input  Cin,
  output Cout,
  output [3:0] S4
);

  wire one_bit_adder_1_cout, one_bit_adder_2_cout, one_bit_adder_3_cout;

  one_bit_adder one_bit_adder_1 (.A(A4[0]), .B(B4[0]), .Cin(Cin), .S(S4[0]), .Cout(one_bit_adder_1_cout));
  one_bit_adder one_bit_adder_2 (
    .A(A4[1]), .B(B4[1]), .Cin(one_bit_adder_1_cout), .S(S4[1]), .Cout(one_bit_adder_2_cout));
  one_bit_adder one_bit_adder_3 (
    .A(A4[2]), .B(B4[2]), .Cin(one_bit_adder_2_cout), .S(S4[2]), .Cout(one_bit_adder_3_cout));
  one_bit_adder one_bit_adder_4 (.A(A4[3]), .B(B4[3]), .Cin(one_bit_adder_3_cout), .S(S4[3]), .Cout(Cout));
endmodule

module sixteen_bit_adder (
  input  [15:0] A16,
  input  [15:0] B16,
  input  Cin,
  output Cout,
  output [15:0] sum
);

  wire four_bit_adder_1_cout, four_bit_adder_2_cout, four_bit_adder_3_cout;

  four_bit_adder four_bit_adder_1 (
    .A4(A16[3:0]), .B4(B16[3:0]), .Cin(Cin), .Cout(four_bit_adder_1_cout), .S4(sum[3:0]));
  four_bit_adder four_bit_adder_2 (
    .A4(A16[7:4]), .B4(B16[7:4]), .Cin(four_bit_adder_1_cout), .Cout(four_bit_adder_2_cout), .S4(sum[7:4]));
  four_bit_adder four_bit_adder_3 (
    .A4(A16[11:8]), .B4(B16[11:8]), .Cin(four_bit_adder_2_cout), .Cout(four_bit_adder_3_cout), .S4(sum[11:8]));
  four_bit_adder four_bit_adder_4 (
    .A4(A16[15:12]), .B4(B16[15:12]), .Cin(four_bit_adder_3_cout), .Cout(Cout), .S4(sum[15:12]));
endmodule
